// Logisim project CustomMultiplier.circ as structural Verilog: 2 circuits, main circuit CustomMultiplier
module CustomMultiplier (
  input  [7:0] FirstOperand,
  input  [7:0] SecondOperand,
  input  Clock,
  input  [7:0] in_4,
  output [7:0] Result,
  output Done
);

  wire comparator_1_eq, comparator_1_lt, or_1_out;
  wire [7:0] customadder_1_result, customadder_2_result, resgiter_2_r;

  CustomAdder customadder_1 (.FirstOperand(FirstOperand), .SecondOperand(Result), .Result(customadder_1_result));
  CustomAdder customadder_2 (.FirstOperand(resgiter_2_r), .SecondOperand(in_4), .Result(customadder_2_result));
  Comparator comparator_1 (
    .a(customadder_2_result), .b(SecondOperand), .gt(Done), .eq(comparator_1_eq), .lt(comparator_1_lt));
  or or_1 (or_1_out, comparator_1_eq, comparator_1_lt);
  resgiter resgiter_1 (.A(customadder_1_result), .load(or_1_out), .clock(Clock), .R(Result));
  resgiter resgiter_2 (.A(customadder_2_result), .load(or_1_out), .clock(Clock), .R(resgiter_2_r));

  // Other names for the same wires on the sheet: A[7:0] = FirstOperand; B[7:0] = SecondOperand; C[7:0] = Result;
  //   clk = Clock
endmodule

module resgiter (
  input  [7:0] A,
  input  load,
  input  clock,
  output [7:0] R
);

  wire multiplexer_1_out, multiplexer_2_out, multiplexer_3_out, multiplexer_4_out, multiplexer_5_out,
       multiplexer_6_out, multiplexer_7_out, multiplexer_8_out;

  Multiplexer multiplexer_1 (.in0(R[0]), .in1(A[0]), .out(multiplexer_1_out), .sel(load));
  Multiplexer multiplexer_2 (.in0(R[1]), .in1(A[1]), .out(multiplexer_2_out), .sel(load));
  Multiplexer multiplexer_3 (.in0(R[2]), .in1(A[2]), .out(multiplexer_3_out), .sel(load));
  Multiplexer multiplexer_4 (.in0(R[5]), .in1(A[5]), .out(multiplexer_4_out), .sel(load));
  Multiplexer multiplexer_5 (.in0(R[6]), .in1(A[6]), .out(multiplexer_5_out), .sel(load));
  Multiplexer multiplexer_6 (.in0(R[7]), .in1(A[7]), .out(multiplexer_6_out), .sel(load));
  D_Flip_Flop d_ff_1 (.D(multiplexer_1_out), .clk(clock), .Q(R[0]));  // open: Qn, preset, reset
  D_Flip_Flop d_ff_2 (.D(multiplexer_2_out), .clk(clock), .Q(R[1]));  // open: Qn, preset, reset
  D_Flip_Flop d_ff_3 (.D(multiplexer_3_out), .clk(clock), .Q(R[2]));  // open: Qn, preset, reset
  D_Flip_Flop d_ff_4 (.D(multiplexer_7_out), .clk(clock), .Q(R[3]));  // open: Qn, preset, reset
  Multiplexer multiplexer_7 (.in0(R[3]), .in1(A[3]), .out(multiplexer_7_out), .sel(load));
  Multiplexer multiplexer_8 (.in0(R[4]), .in1(A[4]), .out(multiplexer_8_out), .sel(load));
  D_Flip_Flop d_ff_5 (.D(multiplexer_5_out), .clk(clock), .Q(R[6]));  // open: Qn, preset, reset
  D_Flip_Flop d_ff_6 (.D(multiplexer_6_out), .clk(clock), .Q(R[7]));  // open: Qn, preset, reset
  D_Flip_Flop d_ff_7 (.D(multiplexer_8_out), .clk(clock), .Q(R[4]));  // open: Qn, preset, reset
  D_Flip_Flop d_ff_8 (.D(multiplexer_4_out), .clk(clock), .Q(R[5]));  // open: Qn, preset, reset
endmodule
